// Logisim project Signal.circ as structural Verilog
module SR_Latch (
  input  R,
  input  S,
  output Q,
  output Not_Q
);

  nor nor_1 (Q, R, Not_Q);
  nor nor_2 (Not_Q, Q, S);
endmodule
