// Logisim project minirv.circ as structural Verilog: 1 circuit, main circuit main
module main (
);

  wire clock_1_out, clock_2_out, clock_3_out, comparator_1_eq, comparator_2_eq, comparator_3_eq,
       comparator_4_eq, decoder_1_out0, decoder_1_out1, decoder_1_out2, decoder_1_out3, decoder_1_out4,
       decoder_1_out5, decoder_1_out6, decoder_1_out7, decoder_1_out8, decoder_1_out9, decoder_1_out10,
       decoder_1_out11, decoder_1_out12, decoder_1_out13, decoder_1_out14, decoder_1_out15, is_addi, is_jalr,
       reset;
  wire [2:0] funct3;
  wire [3:0] rd_selector, rs1_selector, rs2_selector;
  wire [6:0] opcode;
  wire [11:0] I_Type_imm;
  wire [15:0] bit_extender_3_out;
  wire [19:7] RAM_data;
  wire [31:0] adder_1_out, adder_2_out, and_1_out, bit_extender_1_out, bit_extender_2_out, new_PC_data,
       PC_data, rs1_data, rs2_data, write_data, x0_zero_q, x1_ra_q, x2_sp_q, x3_gp_q, x4_tp_q, x5_t0_q,
       x6_t1_q, x7_t2_q, x8_s0_fp_q, x9_s1_q, x10_a0_q, x11_a1_q, x12_a2_q, x13_a3_q, x14_a4_q, x15_a5_q;

  Clock clock_1 (.out(clock_1_out));
  // Probe on write_data
  Clock clock_2 (.out(clock_2_out));
  // NoConnect on decoder_1_out0
  Decoder #(.select(4)) decoder_1 (
    .out0(decoder_1_out0), .out1(decoder_1_out1), .out2(decoder_1_out2), .out3(decoder_1_out3),
    .out4(decoder_1_out4), .out5(decoder_1_out5), .out6(decoder_1_out6), .out7(decoder_1_out7),
    .out8(decoder_1_out8), .out9(decoder_1_out9), .out10(decoder_1_out10), .out11(decoder_1_out11),
    .out12(decoder_1_out12), .out13(decoder_1_out13), .out14(decoder_1_out14), .out15(decoder_1_out15),
    .sel(rd_selector));  // open: en
  Button reset_button (.out(reset));
  Counter #(.max('hffffffff), .width(32)) PC_counter (
    .clr(reset), .load(is_jalr), .up(1'b1), .clk(clock_1_out), .D(new_PC_data), .Q(PC_data));  // open: count, carry
  assign bit_extender_1_out = {{20{I_Type_imm[11]}}, I_Type_imm};  // Bit_Extender bit_extender_1
  assign bit_extender_2_out = {{20{I_Type_imm[11]}}, I_Type_imm};  // Bit_Extender bit_extender_2
  Adder #(.width(32)) adder_1 (.a(bit_extender_1_out), .b(rs1_data), .out(adder_1_out));  // open: cin, cout
  Adder #(.width(32)) adder_2 (.a(bit_extender_2_out), .b(rs1_data), .out(adder_2_out));  // open: cin, cout
  // Probe on write_data
  Register #(.width(32)) x0_zero (.D(write_data), .en(1'b0), .clk(clock_2_out), .Q(x0_zero_q), .clr(1'b1));
  Register #(.width(32)) x8_s0_fp (.D(write_data), .en(decoder_1_out8), .clk(clock_2_out), .Q(x8_s0_fp_q), .clr(reset));
  // Probe on adder_1_out
  Register #(.width(32)) x1_ra (.D(write_data), .en(decoder_1_out1), .clk(clock_2_out), .Q(x1_ra_q), .clr(reset));
  Register #(.width(32)) x9_s1 (.D(write_data), .en(decoder_1_out9), .clk(clock_2_out), .Q(x9_s1_q), .clr(reset));
  // Probe on and_1_out
  assign and_1_out = 32'hfffffffe & adder_2_out;  // AND_Gate and_1, 32 bits wide
  Register #(.width(32)) x2_sp (.D(write_data), .en(decoder_1_out2), .clk(clock_2_out), .Q(x2_sp_q), .clr(reset));
  Register #(.width(32)) x10_a0 (.D(write_data), .en(decoder_1_out10), .clk(clock_2_out), .Q(x10_a0_q), .clr(reset));
  Multiplexer #(.enable("true"), .width(32)) multiplexer_1 (
    .in1(adder_1_out), .out(write_data), .sel(is_addi), .en(is_addi));  // open: in0
  Multiplexer #(.enable("true"), .width(32)) multiplexer_2 (
    .in1(and_1_out), .out(new_PC_data), .sel(is_jalr), .en(is_jalr));  // open: in0
  Register #(.width(32)) x3_gp (.D(write_data), .en(decoder_1_out3), .clk(clock_2_out), .Q(x3_gp_q), .clr(reset));
  Register #(.width(32)) x11_a1 (.D(write_data), .en(decoder_1_out11), .clk(clock_2_out), .Q(x11_a1_q), .clr(reset));
  Register #(.width(32)) x4_tp (.D(write_data), .en(decoder_1_out4), .clk(clock_2_out), .Q(x4_tp_q), .clr(reset));
  Register #(.width(32)) x12_a2 (.D(write_data), .en(decoder_1_out12), .clk(clock_2_out), .Q(x12_a2_q), .clr(reset));
  RAM #(.addrWidth(16), .asyncread("true"), .byteenables("byteEnables"), .dataWidth(32), .\type ("nonvolatile")) ram_1 (
    .addr(bit_extender_3_out), .clk(clock_3_out),
    .dout({I_Type_imm, RAM_data[19:15], funct3, RAM_data[11:7], opcode}));  // open: we, oe, din, be3, be2, be1, be0
  Bit_Extender #(.in_width(32), .\type ("zero")) bit_extender_3 (.in(PC_data), .out(bit_extender_3_out));
  Clock clock_3 (.out(clock_3_out));
  Register #(.width(32)) x5_t0 (.D(write_data), .en(decoder_1_out5), .clk(clock_2_out), .Q(x5_t0_q), .clr(reset));
  Register #(.width(32)) x13_a3 (.D(write_data), .en(decoder_1_out13), .clk(clock_2_out), .Q(x13_a3_q), .clr(reset));
  Register #(.width(32)) x6_t1 (.D(write_data), .en(decoder_1_out6), .clk(clock_2_out), .Q(x6_t1_q), .clr(reset));
  Register #(.width(32)) x14_a4 (.D(write_data), .en(decoder_1_out14), .clk(clock_2_out), .Q(x14_a4_q), .clr(reset));
  Register #(.width(32)) x7_t2 (.D(write_data), .en(decoder_1_out7), .clk(clock_2_out), .Q(x7_t2_q), .clr(reset));
  Register #(.width(32)) x15_a5 (.D(write_data), .en(decoder_1_out15), .clk(clock_2_out), .Q(x15_a5_q), .clr(reset));
  // Probe on {I_Type_imm, RAM_data[19:15], funct3, RAM_data[11:7], opcode}
  Multiplexer #(.select(4), .width(32)) multiplexer_3 (
    .in0(x0_zero_q), .in1(x1_ra_q), .in2(x2_sp_q), .in3(x3_gp_q), .in4(x4_tp_q), .in5(x5_t0_q),
    .in6(x6_t1_q), .in7(x7_t2_q), .in8(x8_s0_fp_q), .in9(x9_s1_q), .in10(x10_a0_q), .in11(x11_a1_q),
    .in12(x12_a2_q), .in13(x13_a3_q), .in14(x14_a4_q), .in15(x15_a5_q), .out(rs1_data), .sel(rs1_selector));
  Multiplexer #(.select(4), .width(32)) multiplexer_4 (
    .in0(x0_zero_q), .in1(x1_ra_q), .in2(x2_sp_q), .in3(x3_gp_q), .in4(x4_tp_q), .in5(x5_t0_q),
    .in6(x6_t1_q), .in7(x7_t2_q), .in8(x8_s0_fp_q), .in9(x9_s1_q), .in10(x10_a0_q), .in11(x11_a1_q),
    .in12(x12_a2_q), .in13(x13_a3_q), .in14(x14_a4_q), .in15(x15_a5_q), .out(rs2_data), .sel(rs2_selector));
  Comparator #(.mode("unsigned"), .width(7)) comparator_1 (
    .a(7'b0010011), .b(opcode), .eq(comparator_1_eq));  // open: gt, lt
  Comparator #(.mode("unsigned"), .width(3)) comparator_2 (
    .a(3'b000), .b(funct3), .eq(comparator_2_eq));  // open: gt, lt
  Comparator #(.mode("unsigned"), .width(7)) comparator_3 (
    .a(7'b1100111), .b(opcode), .eq(comparator_3_eq));  // open: gt, lt
  Comparator #(.mode("unsigned"), .width(3)) comparator_4 (
    .a(3'b000), .b(funct3), .eq(comparator_4_eq));  // open: gt, lt
  Bit_Extender #(.in_width(5), .out_width(4), .\type ("zero")) bit_extender_4 (.in(RAM_data[11:7]), .out(rd_selector));
  and and_2 (is_addi, comparator_1_eq, comparator_2_eq);
  and and_3 (is_jalr, comparator_3_eq, comparator_4_eq);
  Bit_Extender #(.in_width(5), .out_width(4), .\type ("zero")) bit_extender_5 (
    .in(RAM_data[19:15]), .out(rs1_selector));

  // Other names for the same wires on the sheet: RAM_data (some bits) = {I_Type_imm, funct3, opcode};
  //   write_PC = is_jalr

  // Notes on the sheet:
  //   ADDI
  //   JALR
  //   I-Type Parse
endmodule
